# Fritzing sketch Sonar-Project (saved by Fritzing 0.9.5d)
breadboards: 1

parts:
  HC-SR04_Sensor_1 = HC-SR04 Ultrasonic Distance Sensor
  Part1 = Arduino Uno (Rev3)
  LED1 = smd LED [color="Red (633nm)" package="0603 [SMD]"]
  R1 = Resistor [tolerance=±5% resistance=5600 package="2512 [SMD]"]
  J1 = Piezo Speaker

nets:
  VCC: HC-SR04_Sensor_1.VCC, Part1.5V
  N1: HC-SR04_Sensor_1.TRIG, Part1.D2
  N2: HC-SR04_Sensor_1.ECHO, Part1.D3_PWM
  GND: HC-SR04_Sensor_1.GND, Part1.GND, R1.Pin_1, J1.pin1
  N3: Part1.D8, LED1.anode
  N4: Part1.D10_PWM/SS, J1.pin2
  N5: LED1.cathode, R1.Pin_0
